// Digital circuit pong.dig as structural Verilog
module pong (
  input  Master_VGA_Clock,
  input  in_2,
  input  in_3,
  input  in_4,
  input  in_5,
  input  Test_Clock,
  input  in_7,
  input  in_8,
  input  Manual_Clock
);

  wire _7408_1_pin3, _7408_1_pin6, _7408_1_pin8, _7408_1_pin11, _7408_1_pin12, _7408_2_pin3, _7408_2_pin6,
       _7408_2_pin8, _7408_2_pin11, _7408_3_pin3, _7408_3_pin4, _7408_3_pin5, _7408_3_pin6, _7408_4_pin2,
       _7408_4_pin3, _7408_4_pin4, _7408_4_pin5, _7408_4_pin6, _7408_4_pin8, _7408_4_pin11, _7408_4_pin12,
       _7408_4_pin13, _7408_5_pin1, _7408_5_pin2, _7408_5_pin3, _7408_5_pin6, _7408_6_pin3, _7408_6_pin6,
       _7408_6_pin8, _7408_6_pin9, _7408_6_pin10, _7408_6_pin12, _7408_7_pin3, _7408_7_pin9, _7408_7_pin10,
       _7408_7_pin12, _7430_1_pin8, _7430_1_pin12, _7430_3_pin8, _7474_1_pin10, _7474_1_pin13,
       _74163_1_pin15, _74163_2_pin15, _74163_4_pin15, _74163_5_pin15, CLK, H0, H1, H2, H3, H4, H5, H6, H7,
       H8, H9, H10, H11, HCLR, HSYNC, not_1_out, not_2_out, not_13_out, not_14_out, not_15_out, not_16_out,
       not_17_out, not_18_out, not_19_out, not_20_out, not_21_out, not_22_out, not_25_out, not_26_out,
       not_27_out, not_28_out, not_29_out, not_30_out, not_31_out, V0, V1, V2, V3, V4, V5, V6, V7, V8, V9,
       V10, V11, VCLR, VSYNC;

  _74163 _74163_1 (
    .pin1(HCLR), .pin2(CLK), .pin3(1'b0), .pin4(1'b0), .pin5(1'b0), .pin6(1'b0), .pin7(1'b1), .pin8(1'b0),
    .pin9(1'b1), .pin10(1'b1), .pin11(H3), .pin12(H2), .pin13(H1), .pin14(H0), .pin15(_74163_1_pin15),
    .pin16(1'b1));
  _74163 _74163_2 (
    .pin1(HCLR), .pin2(CLK), .pin3(1'b0), .pin4(1'b0), .pin5(1'b0), .pin6(1'b0), .pin7(1'b1), .pin8(1'b0),
    .pin9(1'b1), .pin10(_74163_1_pin15), .pin11(H7), .pin12(H6), .pin13(H5), .pin14(H4),
    .pin15(_74163_2_pin15), .pin16(1'b1));
  _74163 _74163_3 (
    .pin1(HCLR), .pin2(CLK), .pin3(1'b0), .pin4(1'b0), .pin5(1'b0), .pin6(1'b0), .pin7(1'b1), .pin8(1'b0),
    .pin9(1'b1), .pin10(_74163_2_pin15), .pin11(H11), .pin12(H10), .pin13(H9), .pin14(H8), .pin16(1'b1));  // open: pin15
  _74163 _74163_4 (
    .pin1(VCLR), .pin2(HCLR), .pin3(1'b0), .pin4(1'b0), .pin5(1'b0), .pin6(1'b0), .pin7(1'b1), .pin8(1'b0),
    .pin9(1'b1), .pin10(1'b1), .pin11(V3), .pin12(V2), .pin13(V1), .pin14(V0), .pin15(_74163_4_pin15),
    .pin16(1'b1));
  _74163 _74163_5 (
    .pin1(VCLR), .pin2(HCLR), .pin3(1'b0), .pin4(1'b0), .pin5(1'b0), .pin6(1'b0), .pin7(1'b1), .pin8(1'b0),
    .pin9(1'b1), .pin10(_74163_4_pin15), .pin11(V7), .pin12(V6), .pin13(V5), .pin14(V4),
    .pin15(_74163_5_pin15), .pin16(1'b1));
  _74163 _74163_6 (
    .pin1(VCLR), .pin2(HCLR), .pin3(1'b0), .pin4(1'b0), .pin5(1'b0), .pin6(1'b0), .pin7(1'b1), .pin8(1'b0),
    .pin9(1'b1), .pin10(_74163_5_pin15), .pin11(V11), .pin12(V10), .pin13(V9), .pin14(V8), .pin16(1'b1));  // open: pin15
  not not_1 (not_1_out, H7);
  not not_2 (not_2_out, H6);
  _7408 _7408_1 (
    .pin1(H9), .pin2(H8), .pin3(_7408_1_pin3), .pin4(not_1_out), .pin5(not_2_out), .pin6(_7408_1_pin6),
    .pin7(1'b0), .pin8(_7408_1_pin8), .pin9(H3), .pin10(H2), .pin11(_7408_1_pin11), .pin12(_7408_1_pin12),
    .pin13(H4), .pin14(1'b1));
  _7408 _7408_2 (
    .pin1(H1), .pin2(H0), .pin3(_7408_2_pin3), .pin4(_7408_1_pin3), .pin5(_7408_1_pin6), .pin6(_7408_2_pin6),
    .pin7(1'b0), .pin8(_7408_2_pin8), .pin9(_7408_2_pin6), .pin10(_7408_2_pin3), .pin11(_7408_2_pin11),
    .pin12(_7408_1_pin8), .pin13(_7408_1_pin11), .pin14(1'b1));
  not not_3 (_7408_1_pin12, H5);
  // Relay relay_1: pin names not known; wires that end beside it: Master_VGA_Clock, Test_Clock, in_7, in_8, CLK
  // Relay relay_2: pin names not known; wires that end beside it: in_2, 1'b0, CLK, 1'b0, 1'b0
  // Relay relay_3: pin names not known; wires that end beside it: Manual_Clock, CLK
  _7408 _7408_3 (
    .pin1(_7408_2_pin11), .pin2(_7408_2_pin8), .pin3(_7408_3_pin3), .pin4(_7408_3_pin4), .pin5(_7408_3_pin5),
    .pin6(_7408_3_pin6), .pin7(1'b0), .pin9(1'b1), .pin10(1'b1), .pin12(1'b1), .pin13(1'b1), .pin14(1'b1));  // open: pin8, pin11
  not not_4 (HCLR, _7408_3_pin3);
  not not_5 (VCLR, _7408_3_pin6);
  _7408 _7408_4 (
    .pin1(V9), .pin2(_7408_4_pin2), .pin3(_7408_4_pin3), .pin4(_7408_4_pin4), .pin5(_7408_4_pin5),
    .pin6(_7408_4_pin6), .pin7(1'b0), .pin8(_7408_4_pin8), .pin9(V3), .pin10(V2), .pin11(_7408_4_pin11),
    .pin12(_7408_4_pin12), .pin13(_7408_4_pin13), .pin14(1'b1));
  not not_6 (_7408_4_pin2, V8);
  not not_7 (_7408_4_pin4, V7);
  not not_8 (_7408_4_pin5, V6);
  _7408 _7408_5 (
    .pin1(_7408_5_pin1), .pin2(_7408_5_pin2), .pin3(_7408_5_pin3), .pin4(_7408_4_pin3), .pin5(_7408_4_pin6),
    .pin6(_7408_5_pin6), .pin7(1'b0), .pin8(_7408_3_pin5), .pin9(_7408_5_pin6), .pin10(_7408_5_pin3),
    .pin11(_7408_3_pin4), .pin12(_7408_4_pin8), .pin13(_7408_4_pin11), .pin14(1'b1));
  not not_9 (_7408_5_pin1, V1);
  not not_10 (_7408_5_pin2, V0);
  VGA vga_1 (.R(in_3), .G(in_4), .B(in_5), .H(HSYNC), .V(VSYNC), .C(CLK));
  not not_11 (_7408_4_pin13, V4);
  not not_12 (_7408_4_pin12, V5);
  not not_13 (not_13_out, H0);
  not not_14 (not_14_out, H1);
  not not_15 (not_15_out, H2);
  not not_16 (not_16_out, H3);
  not not_17 (not_17_out, H5);
  not not_18 (not_18_out, H8);
  not not_19 (not_19_out, H0);
  not not_20 (not_20_out, H1);
  not not_21 (not_21_out, H2);
  not not_22 (not_22_out, H3);
  _7430 _7430_1 (
    .pin1(not_13_out), .pin2(not_14_out), .pin3(not_15_out), .pin4(not_16_out), .pin5(H4), .pin6(not_17_out),
    .pin7(1'b0), .pin8(_7430_1_pin8), .pin11(H7), .pin12(_7430_1_pin12), .pin14(1'b1));  // open: pin9, pin10, pin13
  _7408 _7408_6 (
    .pin1(not_18_out), .pin2(H9), .pin3(_7408_6_pin3), .pin4(_7430_1_pin8), .pin5(_7408_6_pin3),
    .pin6(_7408_6_pin6), .pin7(1'b0), .pin8(_7408_6_pin8), .pin9(_7408_6_pin9), .pin10(_7408_6_pin10),
    .pin11(_7408_6_pin9), .pin12(_7408_6_pin12), .pin13(H9), .pin14(1'b1));
  _7430 _7430_2 (
    .pin1(not_19_out), .pin2(not_20_out), .pin3(not_21_out), .pin4(not_22_out), .pin5(H4), .pin6(H5),
    .pin7(1'b0), .pin8(_7408_6_pin10), .pin11(H7), .pin12(H6), .pin14(1'b1));  // open: pin9, pin10, pin13
  not not_23 (_7430_1_pin12, H6);
  not not_24 (_7408_6_pin12, H8);
  _7474 _7474_1 (
    .pin1(_7408_6_pin6), .pin2(1'b0), .pin3(1'b0), .pin4(_7408_6_pin8), .pin5(HSYNC), .pin7(1'b0),
    .pin9(VSYNC), .pin10(_7474_1_pin10), .pin11(1'b0), .pin12(1'b0), .pin13(_7474_1_pin13), .pin14(1'b1));  // open: pin6, pin8
  not not_25 (not_25_out, V0);
  not not_26 (not_26_out, V2);
  not not_27 (not_27_out, V4);
  not not_28 (not_28_out, V9);
  not not_29 (not_29_out, V0);
  not not_30 (not_30_out, V1);
  not not_31 (not_31_out, V4);
  _7430 _7430_3 (
    .pin1(not_25_out), .pin2(V1), .pin3(not_26_out), .pin4(V3), .pin5(not_27_out), .pin6(V5), .pin7(1'b0),
    .pin8(_7430_3_pin8), .pin11(V7), .pin12(V6), .pin14(1'b1));  // open: pin9, pin10, pin13
  _7408 _7408_7 (
    .pin1(V8), .pin2(not_28_out), .pin3(_7408_7_pin3), .pin4(_7430_3_pin8), .pin5(_7408_7_pin3),
    .pin6(_7474_1_pin13), .pin7(1'b0), .pin8(_7474_1_pin10), .pin9(_7408_7_pin9), .pin10(_7408_7_pin10),
    .pin11(_7408_7_pin10), .pin12(_7408_7_pin12), .pin13(V8), .pin14(1'b1));
  _7430 _7430_4 (
    .pin1(not_29_out), .pin2(not_30_out), .pin3(V2), .pin4(V3), .pin5(not_31_out), .pin6(V5), .pin7(1'b0),
    .pin8(_7408_7_pin9), .pin11(V7), .pin12(V6), .pin14(1'b1));  // open: pin9, pin10, pin13
  not not_32 (_7408_7_pin12, V9);

  // Notes on the sheet:
  //   Master_VGA_Clock: Hz: 25175000
  //   Test_Clock: Hz: 10000
  //   COUNTERS
  //   I/O SUITE
  //   CLR
  //   VGA DRIVER
  //   SYNC Gen
endmodule
